// Logisim project CPU.circ as structural Verilog: 4 circuits, main circuit DMEM
module DMEM (
  input  [15:0] ADDRESS,
  input  MemWrite,
  input  MemRead,
  input  Clear,
  input  [15:0] DATA_IN,
  input  WORD_EN,
  input  ENDIANNESS,
  output [15:0] DATA_OUT
);

  wire clock_1_out, dmem_control_1_flip_signal, dmem_control_1_sel_0, dmem_control_1_sel_1;
  wire [7:0] ram_1_data, ram_2_data;
  wire [15:0] byte_mirror_1_out, byte_selector_1_word_out;

  Clock clock_1 (.out(clock_1_out));
  BYTE_MIRROR byte_mirror_1 (.IN(DATA_IN), .EN(dmem_control_1_flip_signal), .OUT(byte_mirror_1_out));
  DMEM_CONTROL dmem_control_1 (
    .ENDIANNESS(ENDIANNESS), .WORD_EN(WORD_EN), .FLIP_SIGNAL(dmem_control_1_flip_signal),
    .SEL_0(dmem_control_1_sel_0), .SEL_1(dmem_control_1_sel_1), .A0(ADDRESS[0]));
  RAM #(.addrWidth(15), .bus("separate")) ram_1 (
    .addr(ADDRESS[15:1]), .din(byte_mirror_1_out[7:0]), .data(ram_1_data), .str(MemWrite),
    .sel(dmem_control_1_sel_0), .clk(clock_1_out), .ld(MemRead), .clr(Clear));
  RAM #(.addrWidth(15), .bus("separate")) ram_2 (
    .addr(ADDRESS[15:1]), .din(byte_mirror_1_out[15:8]), .data(ram_2_data), .str(MemWrite),
    .sel(dmem_control_1_sel_1), .clk(clock_1_out), .ld(MemRead), .clr(Clear));
  BYTE_SELECTOR byte_selector_1 (
    .BYTE0(ram_1_data), .EN0(dmem_control_1_sel_0), .BYTE1(ram_2_data), .EN1(dmem_control_1_sel_1),
    .WORD_OUT(byte_selector_1_word_out));
  BYTE_MIRROR byte_mirror_2 (.IN(byte_selector_1_word_out), .EN(dmem_control_1_flip_signal), .OUT(DATA_OUT));
endmodule

module BYTE_MIRROR (
  input  [15:0] IN,
  input  EN,
  output [15:0] OUT
);

  Multiplexer #(.width(8), .enable("false")) multiplexer_1 (.in0(IN[7:0]), .in1(IN[15:8]), .out(OUT[7:0]), .sel(EN));
  Multiplexer #(.width(8), .enable("false")) multiplexer_2 (.in0(IN[15:8]), .in1(IN[7:0]), .out(OUT[15:8]), .sel(EN));
endmodule

module BYTE_SELECTOR (
  input  [7:0] BYTE0,
  input  EN0,
  input  [7:0] BYTE1,
  input  EN1,
  output [15:0] WORD_OUT
);

  Multiplexer #(.width(8), .enable("false")) multiplexer_1 (
    .in0({8{1'b0}}), .in1(BYTE0), .out(WORD_OUT[7:0]), .sel(EN0));
  Multiplexer #(.width(8), .enable("false")) multiplexer_2 (
    .in0({8{1'b0}}), .in1(BYTE1), .out(WORD_OUT[15:8]), .sel(EN1));
endmodule

module DMEM_CONTROL (
  input  A0,
  input  WORD_EN,
  input  ENDIANNESS,
  output SEL_0,
  output SEL_1,
  output FLIP_SIGNAL
);

  or or_1 (SEL_0, ~A0, WORD_EN);  // OR_Gate
  or or_2 (SEL_1, A0, WORD_EN);
  Multiplexer #(.enable("false")) multiplexer_1 (.in0(A0), .in1(ENDIANNESS), .out(FLIP_SIGNAL), .sel(WORD_EN));
endmodule
